# Fritzing sketch L298n (saved by Fritzing 0.9.3b)

parts:
  Bauteil1 = Arduino Uno (Rev3)
  M1 = DC Motor
  S1 = H-Bridge with L298N
  Plattenspieler = Header 5x2 [package=2x5-shrouded_smd]  # not connected
  J1 = Basic Servo
  R1 = Resistor [tolerance=±5% resistance=330 package="0603 [SMD]"]
  R2 = Resistor [tolerance=±5% resistance=220 package="2010 [SMD]"]
  S2 = Tilt Switch [package=THT]

nets:
  N1: Bauteil1.A0, R1.Pin_1, R2.Pin_0
  N2: Bauteil1.D9_PWM, S1.ENA
  N3: Bauteil1.D10_PWM/SS, S2.Pin_1
  N4: Bauteil1.D2, J1.pulse
  N5: Bauteil1.D6_PWM, S1.IN2
  N6: Bauteil1.D7, S1.IN1
  3V3: Bauteil1.3V3, J1.vcc, S2.Pin_2
  GND: Bauteil1.GND, J1.gnd
  N7: M1.pin_1, S1.M1-02
  N8: M1.pin_2, S1.M1-01

notes:
  12 V
  4,3 V
  33 / 45 rpm
  R1: 330 R2: 220 Ohm
  12 V => 4,8 V
  Tilt-Switch

custom parts:
  H-Bridge with L298N: h-bridge
